# Fritzing sketch staci (saved by Fritzing 0.8.5b)
breadboards: 1

parts:
  Part1 = Arduino Mega ADK (Rev3)
  Tiny_RTC1 = Tiny RTC
  S2 = Round Pushbutton
  R1 = Resistor [tolerance=±5% resistance=10k package=THT]
  KEYPAD1 = Membrane Matrix Keypad

nets:
  5V: Part1.5V, Tiny_RTC1.VCC, S2.leg1
  GND: Part1.GND, Tiny_RTC1.GND, S2.leg0, R1.Pin_1
  N1: Part1.D2_PWM, R1.Pin_0
  N2: Part1.D32, KEYPAD1.7
  N3: Part1.D34, KEYPAD1.6
  N4: Part1.D36, KEYPAD1.5
  N5: Part1.D38, KEYPAD1.4
  N6: Part1.D40, KEYPAD1.3
  N7: Part1.D42, KEYPAD1.2
  N8: Part1.D44, KEYPAD1.1

notes:
  1.8TFT SPI 128*160 v1.1 ST7735
  VCC GND CS RST A0 SDA SCK LED
  I2C: SCL SDA
  Serial MP3 Player
  GND VCC TX RX
  4x4 Membrana Keypad

custom parts:
  Tiny RTC: Tiny RTC I2C module DS1370Z RTC and AT24C32 EEPROM
  Membrane Matrix Keypad: Membrane Matrix 3x4 Keypad
